// Logisim project main.circ as structural Verilog: 3 circuits, main circuit main
module main (
);

  wire CLK, DATA, MOV;
  wire [1:0] OP;
  wire [2:0] RD;
  wire [2:1] RA;
  wire [3:0] alu_1_o, controlled_buffer_1_out, counter_1_q, counter_1_q_2, NUM, RegFile_a, RegFile_b;
  wire [15:0] rom_1_data;
  wire [15:9] register_1_q;

  Clock clock_1 (.out(CLK));
  assign controlled_buffer_1_out = MOV ? NUM : 4'bz;  // Controlled_Buffer controlled_buffer_1
  RegFile RegFile (
    .Inp(controlled_buffer_1_out), .C(CLK), .RD(RD), .RA({RA, NUM[3]}), .RB(NUM[2:0]), .A(RegFile_a),
    .B(RegFile_b));
  assign controlled_buffer_1_out = DATA ? alu_1_o : 4'bz;  // Controlled_Buffer controlled_buffer_2
  Hex_Digit_Display hex_digit_display_1 (.value(counter_1_q_2));  // open: dp
  Hex_Digit_Display hex_digit_display_2 (.value(counter_1_q));  // open: dp
  Counter counter_1 (
    .load(1'b0), .count(1'b1), .Q({counter_1_q_2, counter_1_q}), .clk(CLK), .clr(1'b0));  // open: D, carry
  ALU alu_1 (.A(RegFile_a), .B(RegFile_b), .OP(OP), .O(alu_1_o));
  ROM #(.dataWidth(16)) rom_1 (.addr({counter_1_q_2, counter_1_q}), .data(rom_1_data));  // open: sel
  Register #(.width(16)) register_1 (
    .D(rom_1_data), .en(1'b1), .Q({register_1_q[15:14], OP, register_1_q[11:9], RA, NUM, RD}), .clk(CLK));  // open: clr
  and and_1 (DATA, ~register_1_q[14], ~register_1_q[15]);  // AND_Gate
  and and_2 (MOV, register_1_q[14], register_1_q[15]);

  // Other names for the same wires on the sheet: RB[2:0] = NUM[2:0]; RA[0] = NUM[3]
endmodule

module ALU (
  input  [3:0] A,
  input  [3:0] B,
  input  [1:0] OP,
  output [3:0] O
);

  wire [3:0] adder_1_out, and_1_out, or_1_out, xor_1_out;

  Adder #(.width(4)) adder_1 (.a(A), .b(B), .out(adder_1_out), .cin(1'b0));  // open: cout
  assign and_1_out = A & B;  // AND_Gate and_1, 4 bits wide
  assign or_1_out = A | B;  // OR_Gate or_1, 4 bits wide
  assign xor_1_out = A ^ B;  // XOR_Gate xor_1, 4 bits wide
  Multiplexer #(.select(2), .width(4)) multiplexer_1 (
    .in0(adder_1_out), .in1(and_1_out), .in2(or_1_out), .in3(xor_1_out), .out(O), .sel(OP));  // open: en
endmodule

module RegFile (
  input  [3:0] Inp,
  input  C,
  input  [2:0] RA,
  input  [2:0] RD,
  input  [2:0] RB,
  output [3:0] A,
  output [3:0] B
);

  wire demultiplexer_1_out0, demultiplexer_1_out1, demultiplexer_1_out2, demultiplexer_1_out3,
       demultiplexer_1_out4, demultiplexer_1_out5, demultiplexer_1_out6, demultiplexer_1_out7;
  wire [3:0] R0_q, R1_q, R2_q, R3_q, R4_q, R5_q, R6_q, R7_q;

  Demultiplexer #(.select(3), .disabled(0), .enable("false")) demultiplexer_1 (
    .out0(demultiplexer_1_out0), .out1(demultiplexer_1_out1), .out2(demultiplexer_1_out2),
    .out3(demultiplexer_1_out3), .out4(demultiplexer_1_out4), .out5(demultiplexer_1_out5),
    .out6(demultiplexer_1_out6), .out7(demultiplexer_1_out7), .in(1'b1), .sel(RD));
  Register #(.width(4)) R0 (.D(Inp), .en(demultiplexer_1_out0), .Q(R0_q), .clk(C));  // open: clr
  Register #(.width(4)) R1 (.D(Inp), .en(demultiplexer_1_out1), .Q(R1_q), .clk(C));  // open: clr
  Register #(.width(4)) R2 (.D(Inp), .en(demultiplexer_1_out2), .Q(R2_q), .clk(C));  // open: clr
  Register #(.width(4)) R3 (.D(Inp), .en(demultiplexer_1_out3), .Q(R3_q), .clk(C));  // open: clr
  Register #(.width(4)) R4 (.D(Inp), .en(demultiplexer_1_out4), .Q(R4_q), .clk(C));  // open: clr
  Register #(.width(4)) R5 (.D(Inp), .en(demultiplexer_1_out5), .Q(R5_q), .clk(C));  // open: clr
  Register #(.width(4)) R6 (.D(Inp), .en(demultiplexer_1_out6), .Q(R6_q), .clk(C));  // open: clr
  Register #(.width(4)) R7 (.D(Inp), .en(demultiplexer_1_out7), .Q(R7_q), .clk(C));  // open: clr
  Multiplexer #(.select(3), .width(4), .disabled(0), .enable("false")) multiplexer_1 (
    .in0(R0_q), .in1(R1_q), .in2(R2_q), .in3(R3_q), .in4(R4_q), .in5(R5_q), .in6(R6_q), .in7(R7_q), .out(A),
    .sel(RA));
  Multiplexer #(.select(3), .width(4), .disabled(0), .enable("false")) multiplexer_2 (
    .in0(R0_q), .in1(R1_q), .in2(R2_q), .in3(R3_q), .in4(R4_q), .in5(R5_q), .in6(R6_q), .in7(R7_q), .out(B),
    .sel(RB));
endmodule
